# Fritzing sketch SN754410-Bipolar-Stepper-Cntrl (saved by Fritzing 0.8.0b)
breadboards: 1

parts:
  IC1 = H-Bridge [package=THT]
  Q1 = NPN-Transistor [package="TO92 [THT]"]
  Q2 = NPN-Transistor [package="TO92 [THT]"]
  M1 = Stepper Motor - Bipolar
  R2 = Resistor [tolerance=±5% resistance=10k package=THT]
  R3 = Resistor [tolerance=±5% resistance=10k package=THT]

nets:
  N1: IC1.1_2EN, IC1.3_4EN, R2.Pin_0, R3.Pin_1
  N2: IC1.1A, Q1.B
  N3: IC1.1Y, M1.A
  GND1: IC1.GND1, IC1.GND2, IC1.GND3, IC1.GND4, Q1.C, Q2.C
  N4: IC1.2Y, M1.C
  N5: IC1.2A, Q1.E, R2.Pin_1
  N6: IC1.VCC2, IC1.VCC1
  N7: IC1.3A, Q2.E, R3.Pin_0
  N8: IC1.3Y, M1.B
  N9: IC1.4Y, M1.D
  N10: IC1.4A, Q2.B

notes:
  Ctrl1
  Ctrl2
  MVcc
  GND
  5V
