# Fritzing sketch Weather station (saved by Fritzing 0.7.12b)
perfboards: 1

parts:
  Part1 = Ambient Light Sensor (TEMT6000 Breakout Board)
  U1 = atmega328 [package=dip]
  S1 = Pushbutton [package="[THT]"]
  R1 = Resistor [tolerance=±5% resistance=10k package=THT]
  C2 = Ceramic Capacitor [capacitance=22nF package="100 mil [THT, multilayer]"]
  C3 = Ceramic Capacitor [capacitance=22nF package="100 mil [THT, multilayer]"]
  RHT1 = Humidity and Temperature Sensor RHT03
  R2 = Resistor [tolerance=±5% resistance=10k package=THT]
  R3 = Resistor [tolerance=±5% resistance=1k package=THT]
  C4 = Ceramic Capacitor [capacitance=100nF package="100 mil [THT, multilayer]"]
  R4 = Resistor [tolerance=±5% resistance=1k package=THT]
  R5 = Resistor [tolerance=±5% resistance=1k package=THT]
  Part3 = Ethernet Pro  # not connected
  U3 = mystery part, 3 pins [chip_label=3.3v part_number=VR2]
  U4 = mystery part, 3 pins [chip_label=5v part_number=VR1]
  C8 = Ceramic Capacitor [capacitance=100nF package="100 mil [THT, multilayer]"]
  C10 = Electrolytic Capacitor [capacitance=10µF package="100 mil [THT, electrolytic]"]
  D1 = Rectifier Diode [part_number=1N4001 package="300 mil [THT]"]
  C11 = Ceramic Capacitor [capacitance=100nF package="100 mil [THT, multilayer]"]
  C12 = Electrolytic Capacitor [capacitance=10µF package="100 mil [THT, electrolytic]"]
  C13 = Ceramic Capacitor [capacitance=100nF package="100 mil [THT, multilayer]"]
  C14 = Ceramic Capacitor [capacitance=100nF package="100 mil [THT, multilayer]"]
  C15 = Ceramic Capacitor [capacitance=100nF package="100 mil [THT, multilayer]"]
  C16 = Ceramic Capacitor [capacitance=100nF package="100 mil [THT, multilayer]"]
  XTAL1 = Crystal [frequency="16 Mhz" package=THT]
  Power_plug1 = Power plug
  J2 = female pin header, 3 pins [form="♀ (female)"]
  J1 = female pin header, 3 pins [form="♀ (female)"]
  IC1 = IC, DIP package, 4 pins [chip_label=Bar]

nets (from the breadboard view):
  VCC: Part1.VCC, U1.VCC, U1.AVCC, U1.AREF, R1.Pin_1, RHT1.Vcc, R2.Pin_0, R3.Pin_1, C4.0, R4.Pin_1, U4.pin3, C12.+, C13.1, J1.pin3
  N1: Part1.GND, U1.GND#7, S1.Pin_1, S1.Pin_2, C2.1, C3.1, RHT1.GND_1, RHT1.GND_2, C4.1, C12.-, J1.pin1, IC1.pin3
  N2: Part1.S, U1.A1
  N3: U1.RESET, S1.Pin_3, S1.Pin_4, R1.Pin_0, C11.0
  N4: U1.D2, RHT1.Data-signal, R3.Pin_0
  N5: U1.XLAT1, C3.0, XTAL1.pin_0
  N6: U1.XLAT2, C2.0, XTAL1.pin_1
  N7: U1.D6_(PWM), R5.Pin_0
  N8: U1.D7, R4.Pin_0
  N9: U1.D11_(PWM), J1.pin2
  N10: U1.D12, J2.pin1
  N11: U1.D13, J2.pin2
  N12: U1.A0, R2.Pin_1
  N13: U1.A4, IC1.pin2
  N14: U1.A5, IC1.pin1
  N15: U3.pin1, U4.pin1, C8.0, D1.cathode, C14.1, C15.0, C16.0
  N16: U3.pin2, U4.pin2, C8.1, C10.-, C13.0, C14.0, C15.1, C16.1, Power_plug1.GND
  N17: U3.pin3, C10.+, IC1.pin4
  N18: D1.anode, Power_plug1.VCC
  N19: C11.1, J2.pin3

notes:
  Wind Direction
  Wind Speed
  Rain Fall
  Wireless TX SDA out
  Wireless RX SDA in
  Programing Header
  Temp/Humidity
  Ambient Light
  9V
  Gnd
  To LCD
  Wireless TX 12V
  Wireless TX GND
  Wireless RX GND
  Wireless RX 5V
  9V wall adpt
  on the 5V regulator C6 is 0.33 uF so it may need to made with three 0.1 uF caps or even just one
  Controled by ATMega328 on back
  Voltage regulators
  ISP Programing Header
  12V wall adpt
